# Fritzing sketch RemoteController (saved by Fritzing 0.9.3b)
circuit board: 16cm x 10cm
breadboards: 1

parts:
  Part1 = Arduino Nano (Rev3.0)
  R6 = TRIMPOT [package=3362u-2]
  S1 = Momentary Switch [package=ksa_sealed_tac_switch]
  S2 = Momentary Switch [package=ksa_sealed_tac_switch]
  S4 = Momentary Switch [package=ksa_sealed_tac_switch]
  S3 = Momentary Switch [package=ksa_sealed_tac_switch]
  Part3 = NRF24L01+ Breakout Board
  C1 = Capacitor [package=cap-pth-small2]
  Part2 = Adafruit Analog 2-Axis Joystick [part_number="Adafruit #512"]
  R1 = Resistor [tolerance=±2% resistance=220 package="0402 [SMD]"]
  R2 = Resistor [tolerance=±5% resistance=220 package="0402 [SMD]"]
  R4 = Resistor [tolerance=±5% resistance=220 package="0402 [SMD]"]
  R3 = Resistor [tolerance=±5% resistance=220 package="0402 [SMD]"]
  R5 = Resistor [tolerance=±5% resistance=220 package="0402 [SMD]"]
  LCD1 = LCD screen

nets:
  GND: Part1.GND, R6.CCW, Part3.GND, C1.2, Part2.GND, R1.Pin_0, R2.Pin_0, R4.Pin_0, R3.Pin_0, LCD1.VSS, LCD1.R/W, LCD1.LED-
  N1: Part1.D2, S1.1, R1.Pin_1
  N2: Part1.D3, S2.1, R2.Pin_1
  N3: Part1.D4, S4.1, R3.Pin_1
  N4: Part1.D5, LCD1.DB7
  N5: Part1.D6, LCD1.DB6
  N6: Part1.D7, LCD1.DB5
  N7: Part1.D8, LCD1.DB4
  N8: Part1.D9, Part3.CE
  N9: Part1.D10, Part3.CS
  N10: Part1.D11/MOSI, Part3.MOSI
  N11: Part1.D12/MISO, Part3.MISO
  5V: Part1.5V, R6.CW, S1.3, S2.3, S4.3, S3.3, Part2.VCC, R5.Pin_0, LCD1.VDD
  N12: Part1.A5, S3.2
  N13: Part1.A3, Part2.XOUT
  N14: Part1.A2, Part2.YOUT
  N15: Part1.A1, LCD1.E
  N16: Part1.A0, LCD1.RS
  3V3: Part1.3V3, Part3.VCC, C1.1
  N17: Part1.D13/SCK, Part3.SCK
  N18: R6.WIPER, LCD1.V0
  N19: S3.1, R4.Pin_1
  N20: R5.Pin_1, LCD1.LED+

custom parts:
  Adafruit Analog 2-Axis Joystick: This mini-kit makes it easy to mount a PSP/Xbox-like thumb joystick to your project. The thumbstick is an analog joystick - more accurate and sensitive than just 'directional' joysticks - with a 'press in to select' button. Since it's analog, you'll need two analog reading pins on your microcontroller to determine X and Y. Having an extra digital input will let you read the switch. The pack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
