# Fritzing sketch Robot (saved by Fritzing 0.9.3b)
circuit board: 16cm x 10cm
breadboards: 4

parts:
  Part1 = Arduino Nano (Rev3.0) (ICSP)
  IC1 = L293D [package=THT]
  J6 = Screw terminal - 2 pins [package=THT]
  J7 = Screw terminal - 2 pins [package=THT]
  J8 = Screw terminal - 2 pins [package=THT]
  VCC1 = 4 x AAA Battery Mount  # not connected
  VCC2 = 4 x AAA Battery Mount  # not connected
  M2 = DC Motor  # not connected
  M1 = DC Motor  # not connected
  C1 = Capacitor [package=cap-pth-small2]
  Part3 = NRF24L01+ Breakout Board
  GY1 = MPU-6050 Board GY-521 [form="♀ (female)" package=THT]

nets (from the breadboard view):
  GND: Part1.GND, IC1.0V, J6.pin2, C1.2, Part3.GND, GY1.pin2
  N1: Part1.D2, IC1.In_1
  N2: Part1.D3, IC1.Enable_1
  N3: Part1.D4, IC1.In_2
  N4: Part1.D5, IC1.Enable_2
  N5: Part1.D6, IC1.In_4
  N6: Part1.D7, IC1.In_3
  N7: Part1.D9, Part3.CE
  N8: Part1.D10, Part3.CS
  N9: Part1.D11/MOSI, Part3.MOSI
  N10: Part1.D12/MISO, Part3.MISO
  N11: Part1.5V, IC1.+V
  N12: Part1.A5, GY1.pin3
  N13: Part1.A4, GY1.pin4
  3V3: Part1.3V3, C1.1, Part3.VCC, GY1.pin1
  N14: Part1.D13/SCK, Part3.SCK
  N15: IC1.Out_1_(_Controlled_by_Enable_1_), J8.pin2
  N16: IC1.Out_2_(_Controlled_by_Enable_1_), J8.pin1
  N17: IC1.+Vmotor, J6.pin1
  N18: IC1.Out_3_(_Controlled_by_Enable_2_), J7.pin1
  N19: IC1.Out_4_(_Controlled_by_Enable_2_), J7.pin2

custom parts:
  MPU-6050 Board GY-521: Acelerometro y Giroscopio MPU-6050 Board GY-521
